// Logisim project 8_a.circ as structural Verilog: 1 circuit, main circuit main
module main (
  input  in_1,
  input  in_2,
  input  in_3
);

  wire and_1_out, and_2_out, not_1_out, not_2_out, not_3_out, not_4_out, not_5_out, or_1_out, or_2_out,
       or_3_out;

  not not_1 (not_1_out, in_1);
  not not_2 (not_2_out, in_2);
  not not_3 (not_3_out, in_3);
  not not_4 (not_4_out, in_2);
  not not_5 (not_5_out, in_3);
  or or_1 (or_1_out, not_1_out, not_2_out, not_3_out);
  or or_2 (or_2_out, in_1, not_4_out, in_3);
  or or_3 (or_3_out, in_1, in_2, not_5_out);
  and and_1 (and_1_out, or_1_out, or_2_out);
  and and_2 (and_2_out, and_1_out, or_3_out);
  LED led_1 (.in(and_2_out));
endmodule
