// Logisim project Question4.circ as structural Verilog: 1 circuit, main circuit main
module main (
  input  in_1,
  input  in_2,
  input  in_3,
  input  in_4
);

  wire not_2_out, not_3_out, not_4_out, or_2_out;

  // NOT_Gate not_1 has open pins: in=in_1, out=open
  not not_2 (not_2_out, in_3);
  not not_3 (not_3_out, in_2);
  not not_4 (not_4_out, in_4);
  // OR_Gate or_1 has open pins: out=not_2_out
  // OR_Gate or_2 has open pins: out=or_2_out
  _7_Segment_Display u_7_segment_display_1 (
    .f(not_2_out), .a(not_2_out), .b(not_3_out), .d(or_2_out));  // open: g, e, c, dp

  // Notes on the sheet:
  //   gfab
  //   edc.
endmodule
