// Logisim project Lab 9.circ as structural Verilog: 1 circuit, main circuit main
module main (
  input  [3:0] in_1,
  input  [7:0] in_2,
  input  in_3,
  input  in_4,
  input  in_5,
  input  in_6
);

  wire not_1_out;
  wire [7:0] controlled_buffer_3_out, ram_1_data;

  Controlled_Buffer controlled_buffer_1 ();  // open: in, out, en
  ROM rom_1 ();  // open: addr, data, sel
  RAM #(.addrWidth(4)) ram_1 (.addr(in_1), .data(ram_1_data), .sel(in_3), .clk(in_5), .ld(in_4), .clr(in_6));
  assign ram_1_data = not_1_out ? in_2 : 8'bz;  // Controlled_Buffer controlled_buffer_2
  assign controlled_buffer_3_out = in_4 ? ram_1_data : 8'bz;  // Controlled_Buffer controlled_buffer_3
  not not_1 (not_1_out, in_4);
  DotMatrix #(.matrixcols(8), .matrixrows(1)) dotmatrix_1 (
    .col0(controlled_buffer_3_out[7]), .col1(controlled_buffer_3_out[6]), .col2(controlled_buffer_3_out[5]),
    .col3(controlled_buffer_3_out[4]), .col4(controlled_buffer_3_out[3]), .col5(controlled_buffer_3_out[2]),
    .col6(controlled_buffer_3_out[1]), .col7(controlled_buffer_3_out[0]));
endmodule
